# Fritzing sketch Carousel_Wiring_diagram (saved by Fritzing 0.9.3b)

parts:
  VCC1 = Battery
  M1 = DC Motor
  M2 = DC Motor
  S1 = H-Bridge with L298N
  YF-S201_Flow_Meter2 = YF-S201 Water Flow Meter
  Raspberry_Pi_1 = Raspberry Pi 3 [part_number=RPI-3-V1.2]
  YF-S201_Flow_Meter3 = YF-S201 Water Flow Meter
  Componente2 = RFID-RC522-v2

nets:
  GND: VCC1.-, S1.GND, YF-S201_Flow_Meter2.GND, Raspberry_Pi_1.GND, Raspberry_Pi_1.GIPO14, YF-S201_Flow_Meter3.GND, Componente2.GND
  N1: VCC1.+, S1.12V
  N2: M1.pin_1, M2.pin_1, S1.M1-02, S1.M2-02, S1.ENB-5V
  N3: M1.pin_2, S1.M2-01
  N4: M2.pin_2, S1.M1-01
  N5: S1.IN1, Raspberry_Pi_1.GIPO12
  N6: S1.IN2, Raspberry_Pi_1.GIPO13
  N7: S1.IN3, Raspberry_Pi_1.GIPO16
  N8: S1.IN4, Raspberry_Pi_1.GIPO19
  N9: YF-S201_Flow_Meter2.SIG, Raspberry_Pi_1.GIPO18
  VCC: YF-S201_Flow_Meter2.VCC, Raspberry_Pi_1.3v3, YF-S201_Flow_Meter3.VCC, Componente2.3.3V
  N10: Raspberry_Pi_1.GIPO10, Raspberry_Pi_1.GIPO24, Componente2.MOSI
  N11: Raspberry_Pi_1.GIPO9, Componente2.MISO
  N12: Raspberry_Pi_1.GIPO11, Componente2.SCK
  N13: Raspberry_Pi_1.GIPO8, Componente2.SDA
  N14: Raspberry_Pi_1.GIPO25, Componente2.RST
  N15: Raspberry_Pi_1.GIPO23, YF-S201_Flow_Meter3.SIG

notes:
  12 volt power source

custom parts:
  H-Bridge with L298N: h-bridge
  YF-S201 Water Flow Meter: The YF-S201 Flow Meter. The input voltage is 5V to 24V (DC).
  RFID-RC522-v2: A simple China made RFID-RC522 Reader; do check the pin labels, as this is a MFRC522 based clone.
