# Fritzing sketch Carousel_Wiring_diagram_RFID (saved by Fritzing 0.9.3b)

parts:
  Raspberry_Pi_1 = Raspberry Pi 3 [part_number=RPI-3-V1.2]
  Componente2 = RFID-RC522-v2

nets:
  3V3: Raspberry_Pi_1.3v3, Componente2.3.3V
  N1: Raspberry_Pi_1.GIPO10, Componente2.MOSI
  N2: Raspberry_Pi_1.GIPO9, Componente2.MISO
  N3: Raspberry_Pi_1.GIPO11, Componente2.SCK
  N4: Raspberry_Pi_1.GIPO8, Componente2.SDA
  N5: Raspberry_Pi_1.GIPO25, Componente2.RST
  GND: Raspberry_Pi_1.GND, Componente2.GND

custom parts:
  RFID-RC522-v2: A simple China made RFID-RC522 Reader; do check the pin labels, as this is a MFRC522 based clone.
